# Fritzing sketch TwiddleLock (saved by Fritzing 0.9.3b)
breadboards: 1

parts:
  Raspberry_Pi_1 = Raspberry Pi 3 [part_number=RPI-3-V1.2]
  LED2 = LED - 5mm [color="Blue (430nm)" package="5 mm [THT]"]
  ADC1 = MCP3008 [package=dil16]
  U1 = POT [package=pot_alpha_rv16af-20]
  S2 = Pushbutton [package="[THT]"]
  S3 = Pushbutton [package="[THT]"]
  R1 = Resistor [tolerance=±5% resistance=330 package="0603 [SMD]"]
  LED3 = LED - 5mm [color="Red (635nm)" package="5 mm [THT]"]
  R2 = Resistor [tolerance=±5% resistance=220 package="0603 [SMD]"]

nets:
  3V3: Raspberry_Pi_1.3v3, ADC1.VREF, ADC1.VDD, U1.E, S2.Pin_3, S2.Pin_4
  N1: Raspberry_Pi_1.GPIO2, S3.Pin_3
  N2: Raspberry_Pi_1.GPIO3, R2.Pin_0
  N3: Raspberry_Pi_1.GPIO10, ADC1.Din
  N4: Raspberry_Pi_1.GPIO9, ADC1.Dout
  N5: Raspberry_Pi_1.GPIO11, ADC1.CLK
  N6: Raspberry_Pi_1.GPIO19, R1.Pin_0
  N7: Raspberry_Pi_1.GPIO26, S2.Pin_1
  N8: Raspberry_Pi_1.GPIO8, ADC1.CS/SHDN
  N9: Raspberry_Pi_1.GND, LED2.cathode, ADC1.DGND, ADC1.AGND, U1.A, S3.Pin_1, S3.Pin_2, LED3.cathode
  N10: LED2.anode, R1.Pin_1
  N11: ADC1.CH0, U1.S
  N12: LED3.anode, R2.Pin_1
